# Fritzing sketch Attiny85_Writer (saved by Fritzing 0.9.5d)
circuit board: 2.73716cm x 3.26363cm
breadboards: 1

parts:
  IC1 = IC, DIP package, 8 pins [chip_label=IC]
  C1 = Electrolytic Capacitor [capacitance=1µF package="100 mil [THT, electrolytic]"]
  U1 = JST XH 4A 2.54mm [package=THT]
  J1 = Dagu DGServo 9g header (male) [package=THT]

nets:
  N1: IC1.pin1, J1.pulse
  N2: IC1.pin4, C1.-, J1.Vcc
  N3: IC1.pin5, U1.pin1
  N4: IC1.pin6, U1.pin2
  N5: IC1.pin7, U1.pin3
  N6: IC1.pin8, U1.pin4
  N7: C1.+, J1.gnd

notes:
  Rs GND 10
  11 12 13 5V
  ATtiny85 Writer
  →

custom parts:
  JST XH 4A 2.54mm: 4 Pin JST XH connector
