# Fritzing sketch beta_JoyPad (saved by Fritzing 0.9.5d)
circuit board: 8.16937cm x 5.73735cm
breadboards: 1

parts:
  ATtiny85 = IC, DIP package, 8 pins [chip_label=IC]
  SW2_Top = Pushbutton [package="[THT]"]
  SW4_Bottom = Pushbutton [package="[THT]"]
  SW3_Right = Pushbutton [package="[THT]"]
  SW1_Left = Pushbutton [package="[THT]"]
  R1_Left = Resistor [tolerance=±5% resistance=88k package=THT]
  R3_Right = Resistor [tolerance=±5% resistance=33k package=THT]
  R2_Top = Resistor [tolerance=±5% resistance=33k package=THT]
  R4_Bottom = Resistor [tolerance=±5% resistance=88k package=THT]
  R6 = Resistor [tolerance=±5% resistance=22k package=THT]
  R7 = Resistor [tolerance=±5% resistance=22k package=THT]
  SW = Pushbutton [package="[THT]"]
  R8 = Resistor [tolerance=±5% resistance=10k package=THT]
  OLED_I2C1 = OLED 128x64 I2C Monochrome Display
  BAT1 = Battery Holders [package=battcom_20mm_pth]
  S2 = Toggle Switch [package=THT]

nets:
  N1: ATtiny85.pin1, R1_Left.Pin_1, R3_Right.Pin_1, R6.Pin_0
  N2: ATtiny85.pin2, R2_Top.Pin_0, R4_Bottom.Pin_1, R7.Pin_0
  N3: ATtiny85.pin4, SW2_Top.Pin_3, SW2_Top.Pin_4, SW4_Bottom.Pin_1, SW4_Bottom.Pin_2, SW3_Right.Pin_3, SW3_Right.Pin_4, SW1_Left.Pin_3, SW1_Left.Pin_4, SW.Pin_1, SW.Pin_2, OLED_I2C1.GND, BAT1.-
  N4: ATtiny85.pin5, OLED_I2C1.SDA
  N5: ATtiny85.pin6, SW.Pin_3, SW.Pin_4, R8.Pin_1
  N6: ATtiny85.pin7, OLED_I2C1.SCK
  N7: ATtiny85.pin8, R6.Pin_1, R7.Pin_1, R8.Pin_0, OLED_I2C1.VDD, S2.COM
  N8: SW2_Top.Pin_1, SW2_Top.Pin_2, R2_Top.Pin_1
  N9: SW4_Bottom.Pin_3, SW4_Bottom.Pin_4, R4_Bottom.Pin_0
  N10: SW3_Right.Pin_1, SW3_Right.Pin_2, R3_Right.Pin_0
  N11: SW1_Left.Pin_1, SW1_Left.Pin_2, R1_Left.Pin_0
  N12: BAT1.+, S2.L1
